# Fritzing sketch RGBLEDDiagram (Daraghs-MacBook-Pro's conflicted copy 2015-01-21) (saved by Fritzing 0.9.1b)
breadboards: 1

parts:
  U1 = Spark Core (v1.0)
  R1 = Resistor [tolerance=±5% resistance=1k package=THT]
  LED1 = RGB LED - (4 legs) [package="5 mm [THT]"]
  R2 = Resistor [tolerance=±5% resistance=1k package=THT]
  R3 = Resistor [tolerance=±5% resistance=1k package=THT]

nets:
  N1: U1.A0, R3.Pin_1
  N2: U1.A2, U1.3V3, LED1.common_anode
  N3: U1.A3, U1.A6
  N4: U1.A5, U1.VIN
  N5: U1.D0, R1.Pin_1
  N6: U1.D1, R2.Pin_1
  N7: R1.Pin_0, LED1.blue_cathode
  N8: LED1.red_cathode, R3.Pin_0

custom parts:
  Spark Core (v1.0): The Spark Core is a tiny Wi-Fi development board that makes it easy to create internet-connected hardware. The Core is all you need to get started; power it over USB and in minutes you'll be controlling LEDs, switches and motors and collecting data from sensors over the internet! It has 8 digital I/O pins, 8 analog I/O pins, 8 PWM pins; UART (Serial), SPI, I2C, and JTAG peripherals available.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
