# Fritzing sketch TMP36Diagram (saved by Fritzing 0.9.1b)
breadboards: 1

parts:
  U1 = Spark Core (v1.0)
  T1 = TMP36 Temperature Sensor [package="TO92 [THT]"]
  C1 = Ceramic Capacitor [capacitance=10nF voltage=6.3V package="200 mil [THT, multilayer]"]

nets:
  N1: U1.A0, T1.Vout, C1.1
  N2: U1.A2, U1.3V3
  N3: U1.A3, U1.A6
  N4: U1.A5, U1.VIN
  GND: U1.GND, T1.GND, C1.0
  N5: U1.3V3*, T1.+Vs

custom parts:
  Spark Core (v1.0): The Spark Core is a tiny Wi-Fi development board that makes it easy to create internet-connected hardware. The Core is all you need to get started; power it over USB and in minutes you'll be controlling LEDs, switches and motors and collecting data from sensors over the internet! It has 8 digital I/O pins, 8 analog I/O pins, 8 PWM pins; UART (Serial), SPI, I2C, and JTAG peripherals available.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
