# Fritzing sketch Motion (saved by Fritzing 0.9.1b)
breadboards: 1

parts:
  U1 = Spark Core (v1.0)
  LED1 = LED - 5mm [color="Red (633nm)" package="5 mm [THT]"]
  R1 = Resistor [tolerance=±5% resistance=1k package=THT]
  PIR1 = PIR sensor

nets:
  N1: U1.A2, U1.3V3
  N2: U1.A3, U1.A6
  VIN: U1.A5, U1.VIN, PIR1.VDD
  GND: U1.GND, LED1.cathode, PIR1.GND
  N3: U1.D0, PIR1.SIG
  N4: U1.D1, R1.Pin_1
  N5: LED1.anode, R1.Pin_0

custom parts:
  Spark Core (v1.0): The Spark Core is a tiny Wi-Fi development board that makes it easy to create internet-connected hardware. The Core is all you need to get started; power it over USB and in minutes you'll be controlling LEDs, switches and motors and collecting data from sensors over the internet! It has 8 digital I/O pins, 8 analog I/O pins, 8 PWM pins; UART (Serial), SPI, I2C, and JTAG peripherals available.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
