# Fritzing sketch Pot (saved by Fritzing 0.9.1b)
breadboards: 1

parts:
  U1 = Spark Core (v1.0)
  LED1 = LED - 5mm [color="Red (633nm)" package="5 mm [THT]"]
  R1 = Resistor [tolerance=±5% resistance=1k package=THT]
  R2 = Rotary Potentiometer (Small) [maximum_resistance=100kΩ package=THT]

nets:
  N1: U1.A0, R2.wiper
  N2: U1.A2, U1.3V3
  N3: U1.A3, U1.A6
  N4: U1.A5, U1.VIN, R2.leg2
  N5: U1.GND, LED1.cathode, R2.leg1
  N6: U1.D1, R1.Pin_1
  N7: LED1.anode, R1.Pin_0

custom parts:
  Spark Core (v1.0): The Spark Core is a tiny Wi-Fi development board that makes it easy to create internet-connected hardware. The Core is all you need to get started; power it over USB and in minutes you'll be controlling LEDs, switches and motors and collecting data from sensors over the internet! It has 8 digital I/O pins, 8 analog I/O pins, 8 PWM pins; UART (Serial), SPI, I2C, and JTAG peripherals available.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
