# Fritzing sketch Servo (saved by Fritzing 0.9.1b)
breadboards: 1

parts:
  U1 = Spark Core (v1.0)
  J1 = Basic Servo

nets:
  N1: U1.A2, U1.3V3
  N2: U1.A3, U1.A6
  VIN: U1.A5, U1.VIN, J1.vcc
  N3: U1.A7, J1.pulse
  GND: U1.GND, J1.gnd

custom parts:
  Spark Core (v1.0): The Spark Core is a tiny Wi-Fi development board that makes it easy to create internet-connected hardware. The Core is all you need to get started; power it over USB and in minutes you'll be controlling LEDs, switches and motors and collecting data from sensors over the internet! It has 8 digital I/O pins, 8 analog I/O pins, 8 PWM pins; UART (Serial), SPI, I2C, and JTAG peripherals available.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
