# Fritzing sketch ConnectedDoorbell (saved by Fritzing 0.9.1b)
breadboards: 1

parts:
  U1 = Spark Core (v1.0)
  S1 = Pushbutton [package="[THT]"]
  J1 = Piezo Speaker

nets:
  N1: U1.A0, J1.pin2
  N2: U1.A2, U1.3V3
  N3: U1.A3, U1.A6
  N4: U1.A5, U1.VIN
  N5: U1.GND, S1.Pin_3, S1.Pin_4, J1.pin1
  N6: U1.D0, S1.Pin_1, S1.Pin_2

custom parts:
  Spark Core (v1.0): The Spark Core is a tiny Wi-Fi development board that makes it easy to create internet-connected hardware. The Core is all you need to get started; power it over USB and in minutes you'll be controlling LEDs, switches and motors and collecting data from sensors over the internet! It has 8 digital I/O pins, 8 analog I/O pins, 8 PWM pins; UART (Serial), SPI, I2C, and JTAG peripherals available.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
